# Fritzing sketch PiAlarm (saved by Fritzing 0.9.3b)
circuit board: 8.46667cm x 5.64444cm
breadboards: 1

parts:
  IC1 = L293D [package=THT]
  U1 = Voltage Regulator - 5V [package="TO220 [THT]"]
  Part1 = Adafruit Pi Cobbler [part_number="Adafruit #914"]
  Part2 = Adafruit ADS1015 12Bit I2C ADC [part_number="Adafruit #1083"]
  JACK1 = 2.1mm DC Barrel Jack
  Part4 = Adafruit DS1307 RTC Breakout [part_number="Adafruit #264"]
  JACK2 = 2.1mm DC Barrel Jack
  TRS1 = Audio Jack (TRS) 3.5mm [package="PG203J [THT]"]
  R1 = Resistor [tolerance=±5% resistance=1k package=THT]
  R2 = PHOTOCELL [package=photocell-kit]
  R3 = Resistor [tolerance=±5% resistance=1k package=THT]

nets:
  VDD: IC1.Enable_1, IC1.+V, Part1.5.0V, Part2.VDD, Part4.VCC, R2.P$1
  N1: IC1.In_1, Part1.GPIO25
  N2: IC1.Out_1_(_Controlled_by_Enable_1_), JACK2.center
  GND: IC1.0V, IC1.In_2, U1.GND, Part1.GND, Part2.GND, JACK1.sleeve, Part4.GND, JACK2.sleeve, R1.Pin_0, R3.Pin_0
  N3: IC1.+Vmotor, U1.input_voltage, JACK1.center
  N4: Part1.SDA, Part2.SDA, Part4.SDA
  N5: Part1.SCL, Part2.SCL, Part4.SCL
  N6: Part2.AIN1, R2.P$2, R3.Pin_1
  N7: Part2.AIN0, TRS1.Ring, R1.Pin_1

notes:
  Solder a MicroUSB connector to these wires to power the Pi
  Plug any 12v adapter in here.
  Plug in the bed shaker here, no modification required.
  Solder a headphone connector on the pressure pad and plug in here, if you have one.

custom parts:
  Adafruit Pi Cobbler: Now that you've finally got your hands on a Raspberry Pi® Model B , you're probably itching to make some fun embedded computer projects with it. What you need is an add on prototyping Pi Cobbler from Adafruit, which can break out all those tasty power, GPIO, I2C and SPI pins from the 26 pin header onto a solderless breadboard. This set will make "cobbling together" prototypes with the Pi super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
  Adafruit ADS1015 12Bit I2C ADC: For microcontrollers without an analog-to-digital converter or when you want a higher-precision ADC, the ADS1015 provides 12-bit precision at 3300 samples/second over I2C. The chip can be configured as 4 single-ended input channels, or two differential channels. As a nice bonus, it even includes a programmable gain amplifier, up to x16, to help boost up smaller single/differential signals to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
  2.1mm DC Barrel Jack: 2.1mm DC Barrel Jack with Thru-Hole Connectors (breadboardable)
  Adafruit DS1307 RTC Breakout: This is a great battery-backed real time clock (RTC) that allows your microcontroller project to keep track of time even if it is reprogrammed, or if the power is lost. Perfect for datalogging, clock-building, time stamping, timers and alarms, etc. The DS1307 is the most popular RTC - but it requires 5V power to work (although we've used it with 5V power and 3.3V logic successfully) PCB &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
